# Fritzing sketch H-bridge_Intro (saved by Fritzing 0.9.3b)
breadboards: 1

parts:
  S2 = H-Bridge with L298N
  M2 = DC Motor
  Part1 = Arduino Uno (Rev3)
  BAT1 = BC9VPC [package=bc9vpc]

nets:
  N1: S2.12V, BAT1.V+
  GND: S2.GND, Part1.GND, BAT1.V-
  N2: S2.IN1, Part1.D4
  N3: S2.IN2, Part1.D5_PWM
  N4: S2.M1-01, M2.pin_2
  N5: S2.M1-02, M2.pin_1

custom parts:
  H-Bridge with L298N: h-bridge
