# Fritzing sketch Stupidcar_wEnables (saved by Fritzing 0.9.3b)
breadboards: 1

parts:
  Part1 = Arduino Uno (Rev3)
  S1 = H-Bridge with L298N
  M1 = DC Motor
  M2 = DC Motor
  BAT1 = BC9VPC [package=bc9vpc]

nets:
  N1: Part1.D9_PWM, S1.ENB
  GND: Part1.GND, S1.GND, BAT1.V-
  N2: Part1.D3_PWM, S1.ENA
  N3: Part1.D4, S1.IN1
  N4: Part1.D5_PWM, S1.IN2
  N5: Part1.D6_PWM, S1.IN3
  N6: Part1.D7, S1.IN4
  VIN: Part1.VIN, S1.12V, BAT1.V+
  N7: S1.M1-01, M2.pin_2
  N8: S1.M1-02, M2.pin_1
  N9: S1.M2-01, M1.pin_2
  N10: S1.M2-02, M1.pin_1

custom parts:
  H-Bridge with L298N: h-bridge
