# Fritzing sketch Linebot (saved by Fritzing 0.9.3b)
breadboards: 1

parts:
  Part1 = Arduino Uno (Rev3)
  S1 = H-Bridge with L298N
  M1 = DC Motor
  M2 = DC Motor
  M3 = fc-51 [package=THT]
  M4 = fc-51 [package=THT]
  HC-SR04_Sensor_1 = HC-SR04 Ultrasonic Distance Sensor
  BAT1 = BC9VPC [package=bc9vpc]

nets:
  N1: Part1.D9_PWM, S1.ENB
  N2: Part1.D10_PWM/SS, M3.pin1
  N3: Part1.D11_PWM/MOSI, HC-SR04_Sensor_1.ECHO
  N4: Part1.D12/MISO, HC-SR04_Sensor_1.TRIG
  N5: Part1.D13/SCK, M4.pin1
  GND: Part1.GND, S1.GND, M3.pin2, M4.pin2, HC-SR04_Sensor_1.GND, BAT1.V-
  N6: Part1.D3_PWM, S1.ENA
  N7: Part1.D4, S1.IN1
  N8: Part1.D5_PWM, S1.IN2
  N9: Part1.D6_PWM, S1.IN3
  N10: Part1.D7, S1.IN4
  5V: Part1.5V, M3.pin3, M4.pin3, HC-SR04_Sensor_1.VCC
  VIN: Part1.VIN, S1.12V, BAT1.V+
  N11: S1.M1-01, M2.pin_2
  N12: S1.M1-02, M2.pin_1
  N13: S1.M2-01, M1.pin_2
  N14: S1.M2-02, M1.pin_1

custom parts:
  H-Bridge with L298N: h-bridge
